# Fritzing sketch Circuit Diagram (saved by Fritzing 0.9.3b)

parts:
  Part1 = Lithium Ion Polymer Battery 3.7v 1200mAh [part_number=258]
  Part2 = Lithium Ion Polymer Battery 3.7v 1200mAh [part_number=258]
  Part3 = Lithium Ion Polymer Battery 3.7v 1200mAh [part_number=258]
  PWM1 = PCA9685 16x12-bit PWM Breakout
  MH-ET_LIVE_ESP32_DEVKIT1 = MH-ET LIVE ESP32 DEVKIT 38 pins
  U1 = LM2596 step down module
  SERVO1 = Tower Pro SG90 servo [part_number=101246]
  SERVO2 = Tower Pro SG90 servo [part_number=101246]
  SERVO3 = Tower Pro SG90 servo [part_number=101246]
  SERVO4 = Tower Pro SG90 servo [part_number=101246]
  SERVO5 = Tower Pro SG90 servo [part_number=101246]
  SERVO6 = Tower Pro SG90 servo [part_number=101246]
  hc-sr1 = hc-sr04
  M1 = fc-51 [package=THT]

nets:
  N1: Part1.positive, U1.IN+
  N2: Part1.negative, Part2.positive
  N3: Part2.negative, Part3.positive
  GND: Part3.negative, PWM1.no_name_yet#501, PWM1.no_name_yet#701, PWM1.no_name_yet#1000, PWM1.no_name_yet#1001, PWM1.no_name_yet#1002, PWM1.no_name_yet#1003, PWM1.no_name_yet#1004, PWM1.no_name_yet#1005, PWM1.no_name_yet#1013, PWM1.no_name_yet#1014, PWM1.no_name_yet#1015, MH-ET_LIVE_ESP32_DEVKIT1.GND, U1.IN-, U1.OUT-, SERVO1.GND, SERVO2.GND, SERVO3.GND, SERVO4.GND, SERVO5.GND, SERVO6.GND, hc-sr1.GND, M1.pin2
  N4: PWM1.no_name_yet#0, SERVO6.Signal
  N5: PWM1.no_name_yet#1, SERVO5.Signal
  N6: PWM1.no_name_yet#2, SERVO4.Signal
  N7: PWM1.no_name_yet#3, SERVO3.Signal
  N8: PWM1.no_name_yet#5, SERVO1.Signal, SERVO2.Signal
  +5V: PWM1.no_name_yet#100, PWM1.no_name_yet#101, PWM1.no_name_yet#102, PWM1.no_name_yet#103, PWM1.no_name_yet#104, PWM1.no_name_yet#105, PWM1.no_name_yet#111, PWM1.no_name_yet#115, PWM1.no_name_yet#506, PWM1.no_name_yet#706, MH-ET_LIVE_ESP32_DEVKIT1.5V, U1.OUT+, SERVO1.+5V, SERVO2.+5V, SERVO3.+5V, SERVO4.+5V, SERVO5.+5V, SERVO6.+5V, hc-sr1.VCC, M1.pin3
  N9: PWM1.no_name_yet#503, MH-ET_LIVE_ESP32_DEVKIT1.IO22
  N10: PWM1.no_name_yet#505, MH-ET_LIVE_ESP32_DEVKIT1.3V3
  N11: MH-ET_LIVE_ESP32_DEVKIT1.IO32, hc-sr1.Trig
  N12: MH-ET_LIVE_ESP32_DEVKIT1.IO33, hc-sr1.Echo
  N13: MH-ET_LIVE_ESP32_DEVKIT1.IO19, M1.pin1

notes:
  SCL -> IO21
  SDA-> IO22
  Trig-> IO32
  Echo->IO33
  OUT-> IO19
  Connect Servos as You Like and change the code accordingly.
  Made By :
  Dinul Sasnada

custom parts:
  Lithium Ion Polymer Battery 3.7v 1200mAh: Lithium ion polymer (also known as 'lipo' or 'lipoly') batteries are thin, light and powerful. The output ranges from 4.2V when completely charged to 3.7V. This battery has a capacity of 1200mAh for a total of about 4.5 Wh. The batteries come pre-attached with a genuine 2-pin JST-PH connector as shown and include the necessary protection circuitry.
  MH-ET LIVE ESP32 DEVKIT 38 pins: http://mh.nodebb.com/topic/2/mh-et-live-esp32-devkit
  LM2596 step down module: LM2596 DC-DC step down power supply module 3 A.
  Tower Pro SG90 servo: Original file by John De Cristofaro http://www.adafruit.com/products/1449 Adafruit Feedback Servo (Small) Edited by: e-radionica.com 28/9/2015
